# Fritzing sketch projekt (saved by Fritzing 0.9.2b)
breadboards: 1

parts:
  Part1 = Arduino Uno (Rev3) - ICSP
  Nokia_5110_LCD_Module1 = Nokia 5110 LCD
  U4 = EM408_CON [package=em408_con]

nets:
  GND: Part1.GND, Nokia_5110_LCD_Module1.GND, Nokia_5110_LCD_Module1.LED, Nokia_5110_LCD_Module1.GND_(out), Nokia_5110_LCD_Module1.LED_(out), U4.GND
  N1: Part1.D9_PWM, Nokia_5110_LCD_Module1.RST, Nokia_5110_LCD_Module1.RST_(out)
  N2: Part1.D10_PWM/SS, Nokia_5110_LCD_Module1.SCE, Nokia_5110_LCD_Module1.SCE_(out)
  N3: Part1.D11_PWM/MOSI, Nokia_5110_LCD_Module1.D/C, Nokia_5110_LCD_Module1.D/C_(out)
  N4: Part1.D12/MISO, Nokia_5110_LCD_Module1.DN(MOSI), Nokia_5110_LCD_Module1.DN(MODI)_(out)
  N5: Part1.D13/SCK, Nokia_5110_LCD_Module1.SCLK, Nokia_5110_LCD_Module1.SCLK_(out)
  N6: Part1.D0/RX, U4.TX
  N7: Part1.D1/TX, U4.RX
  VCC: Part1.3V3, Nokia_5110_LCD_Module1.VCC, Nokia_5110_LCD_Module1.VCC_(out), U4.VCC

custom parts:
  Nokia 5110 LCD: Nokia 5110 Graphic 84*48 LCD module such as the Sparkfun LCD-10168 or the clones from Ebay. There is example code for the Arduino available from the Sparkfun site in https://learn.sparkfun.com/tutorials/graphic-lcd-hookup-guide This is a 3.3V device, if you are running it from a 5V micro you need a 5V tolorant level translator such as the 74ahc367 to protect the signal imputs. Rafa G. did a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
